# Fritzing sketch candle-lights (saved by Fritzing 0.9.1b)
breadboards: 1

parts:
  パーツ1 = Arduino Due (Rev2b)
  LED1 = LED - 5mm [color="Red (633nm)" package="5 mm [THT]"]

nets:
  N1: パーツ1.D9_PWM, LED1.anode
  N2: パーツ1.SDA1, LED1.cathode
